// Logisim project 24h_clock.circ as structural Verilog: 1 circuit, main circuit main
module main (
);

  wire and_2_out, and_3_out, and_4_out, and_5_out, and_6_out, and_7_out, and_8_out, and_9_out, and_10_out,
       and_11_out, and_12_out, and_13_out, and_14_out, and_15_out, and_16_out, and_17_out, and_18_out,
       and_19_out, and_20_out, and_21_out, and_22_out, and_23_out, and_24_out, and_25_out, and_26_out,
       and_27_out, and_28_out, and_29_out, and_30_out, and_31_out, and_32_out, and_33_out, and_34_out,
       and_35_out, and_36_out, and_37_out, and_38_out, and_39_out, clock_1_out, j_k_ff_1_q, j_k_ff_2_q,
       j_k_ff_2_qn, j_k_ff_3_q, j_k_ff_4_q, j_k_ff_4_qn, j_k_ff_5_q, j_k_ff_6_q, j_k_ff_6_qn, j_k_ff_7_q,
       j_k_ff_7_qn, j_k_ff_8_q, j_k_ff_9_q, j_k_ff_10_q, j_k_ff_10_qn, j_k_ff_11_q, j_k_ff_11_qn,
       j_k_ff_12_q, j_k_ff_12_qn, j_k_ff_13_q, j_k_ff_14_q, j_k_ff_14_qn, j_k_ff_15_q, j_k_ff_15_qn,
       j_k_ff_16_q, not_1_out, not_2_out, not_3_out, not_4_out, not_5_out, not_6_out, not_7_out, not_8_out,
       not_9_out, not_10_out, not_11_out, not_12_out, not_13_out, not_14_out, not_15_out, not_16_out,
       or_1_out, or_2_out, or_3_out, or_4_out, or_5_out, or_6_out, or_7_out, or_8_out, or_9_out, or_10_out,
       or_11_out, or_12_out, or_13_out, or_14_out, or_15_out, or_16_out, or_17_out, or_18_out, or_19_out,
       or_20_out, or_21_out, or_22_out, or_23_out, or_24_out, or_25_out, or_26_out, or_27_out, or_28_out,
       or_29_out, or_30_out, or_31_out, P_R_out, P_RSa_out, PaQa_out, PaQaR_out, QaSa_out, QQ_out, QRa_out,
       QRaS_out, QS_out, QSa_out, RaSa_out, RS_out, RSa_out;

  _7_Segment_Display #(.decimalPoint("false")) u_7_segment_display_1 ();  // open: g, f, a, b, e, d, c
  // AND_Gate and_1 has open pins: in0=and_11_out, in1=j_k_ff_4_qn, in2=j_k_ff_2_qn, in3=j_k_ff_3_q, in4=j_k_ff_1_q, out=open
  Clock clock_1 (.out(clock_1_out));
  _7_Segment_Display u_7_segment_display_2 ();  // open: g, f, a, b, e, d, c, dp
  J_K_Flip_Flop j_k_ff_1 (
    .J(and_11_out), .K(and_11_out), .clk(clock_1_out), .Q(j_k_ff_1_q), .reset(and_2_out));  // open: Qn, preset
  not not_1 (not_1_out, j_k_ff_1_q);
  and and_2 (and_2_out, j_k_ff_2_q, j_k_ff_3_q);
  not not_2 (not_2_out, j_k_ff_2_q);
  and and_3 (and_3_out, and_11_out, j_k_ff_1_q);
  J_K_Flip_Flop j_k_ff_2 (
    .J(and_3_out), .K(and_3_out), .clk(clock_1_out), .Q(j_k_ff_2_q), .Qn(j_k_ff_2_qn), .reset(and_2_out));  // open: preset
  not not_3 (not_3_out, j_k_ff_3_q);
  not not_4 (not_4_out, j_k_ff_4_q);
  and and_4 (and_4_out, and_3_out, j_k_ff_2_q);
  J_K_Flip_Flop j_k_ff_3 (
    .J(and_4_out), .K(and_4_out), .clk(clock_1_out), .Q(j_k_ff_3_q), .reset(and_2_out));  // open: Qn, preset
  and and_5 (and_5_out, j_k_ff_3_q, j_k_ff_1_q);
  and and_6 (and_6_out, not_3_out, not_1_out);
  and and_7 (and_7_out, not_4_out, not_3_out);
  and and_8 (and_8_out, not_2_out, not_1_out);
  or or_1 (or_1_out, j_k_ff_4_q, j_k_ff_3_q, not_2_out, j_k_ff_1_q);
  and and_9 (and_9_out, j_k_ff_2_q, not_1_out);
  or or_2 (or_2_out, j_k_ff_3_q, j_k_ff_2_q);
  and and_10 (and_10_out, and_4_out, j_k_ff_3_q);
  or or_3 (or_3_out, and_5_out, and_6_out);
  J_K_Flip_Flop j_k_ff_4 (
    .J(and_10_out), .K(and_10_out), .clk(clock_1_out), .Q(j_k_ff_4_q), .Qn(j_k_ff_4_qn), .reset(and_2_out));  // open: preset
  _7_Segment_Display #(.decimalPoint("false")) u_7_segment_display_3 (
    .g(or_2_out), .f(or_6_out), .a(or_4_out), .b(or_5_out), .e(or_7_out), .d(or_4_out), .c(or_1_out));
  or or_4 (or_4_out, j_k_ff_2_q, or_3_out);
  or or_5 (or_5_out, and_7_out, and_8_out);
  or or_6 (or_6_out, and_8_out, j_k_ff_3_q);
  or or_7 (or_7_out, and_6_out, and_9_out);
  and and_11 (and_11_out, j_k_ff_8_q, j_k_ff_7_qn, and_26_out, j_k_ff_6_qn, j_k_ff_5_q);
  _7_Segment_Display u_7_segment_display_4 (
    .g(or_16_out), .f(or_17_out), .a(or_10_out), .b(or_11_out), .e(or_12_out), .d(or_15_out), .c(or_9_out),
    .dp(1'b1));
  not not_5 (not_5_out, j_k_ff_5_q);
  not not_6 (not_6_out, j_k_ff_6_q);
  not not_7 (not_7_out, j_k_ff_7_q);
  J_K_Flip_Flop j_k_ff_5 (
    .J(and_26_out), .K(and_26_out), .clk(clock_1_out), .Q(j_k_ff_5_q), .reset(and_13_out));  // open: Qn, preset
  not not_8 (not_8_out, j_k_ff_8_q);
  and and_12 (and_12_out, and_26_out, j_k_ff_5_q);
  and and_13 (and_13_out, j_k_ff_6_q, j_k_ff_8_q);
  or or_8 (or_8_out, j_k_ff_8_q, j_k_ff_6_q);
  and and_14 (and_14_out, j_k_ff_7_q, j_k_ff_5_q);
  and and_15 (and_15_out, not_7_out, not_5_out);
  and and_16 (and_16_out, not_8_out, not_7_out);
  and and_17 (and_17_out, not_6_out, not_5_out);
  and and_18 (and_18_out, j_k_ff_6_q, j_k_ff_5_q);
  or or_9 (or_9_out, j_k_ff_8_q, j_k_ff_7_q, not_6_out, j_k_ff_5_q);
  and and_19 (and_19_out, j_k_ff_6_q, not_5_out);
  and and_20 (and_20_out, j_k_ff_7_q, not_6_out);
  and and_21 (and_21_out, j_k_ff_7_q, not_5_out);
  J_K_Flip_Flop j_k_ff_6 (
    .J(and_12_out), .K(and_12_out), .clk(clock_1_out), .Q(j_k_ff_6_q), .Qn(j_k_ff_6_qn), .reset(and_13_out));  // open: preset
  and and_22 (and_22_out, and_12_out, j_k_ff_6_q);
  J_K_Flip_Flop j_k_ff_7 (
    .J(and_22_out), .K(and_22_out), .clk(clock_1_out), .Q(j_k_ff_7_q), .Qn(j_k_ff_7_qn), .reset(and_13_out));  // open: preset
  or or_10 (or_10_out, or_8_out, and_14_out, and_15_out);
  or or_11 (or_11_out, j_k_ff_8_q, and_16_out, and_17_out, and_18_out);
  or or_12 (or_12_out, and_15_out, and_19_out);
  or or_13 (or_13_out, j_k_ff_8_q, and_19_out);
  and and_23 (and_23_out, j_k_ff_5_q, and_20_out);
  and and_24 (and_24_out, and_16_out, j_k_ff_6_q);
  or or_14 (or_14_out, and_17_out, j_k_ff_8_q);
  or or_15 (or_15_out, and_15_out, or_13_out, and_23_out, and_24_out);
  or or_16 (or_16_out, or_13_out, and_24_out, and_20_out);
  or or_17 (or_17_out, or_14_out, and_20_out, and_21_out);
  and and_25 (and_25_out, and_22_out, j_k_ff_7_q);
  J_K_Flip_Flop j_k_ff_8 (
    .J(and_25_out), .K(and_25_out), .clk(clock_1_out), .Q(j_k_ff_8_q), .reset(and_13_out));  // open: Qn, preset
  _7_Segment_Display #(.decimalPoint("false")) u_7_segment_display_5 (
    .g(or_19_out), .f(or_23_out), .a(or_21_out), .b(or_22_out), .e(or_24_out), .d(or_21_out), .c(or_18_out));
  _7_Segment_Display #(.decimalPoint("false")) u_7_segment_display_6 (
    .g(or_30_out), .f(or_31_out), .a(or_25_out), .b(or_26_out), .e(or_27_out), .d(or_29_out), .c(or_20_out));
  and and_26 (and_26_out, j_k_ff_12_qn, j_k_ff_11_q, and_36_out, j_k_ff_10_qn, j_k_ff_9_q);
  J_K_Flip_Flop j_k_ff_9 (
    .J(and_36_out), .K(and_36_out), .clk(clock_1_out), .Q(j_k_ff_9_q), .reset(and_27_out));  // open: Qn, preset
  not not_9 (not_9_out, j_k_ff_13_q);
  not not_10 (not_10_out, j_k_ff_9_q);
  not not_11 (not_11_out, j_k_ff_10_q);
  and and_27 (and_27_out, j_k_ff_10_q, j_k_ff_11_q);
  not not_12 (not_12_out, j_k_ff_14_q);
  not not_13 (not_13_out, j_k_ff_11_q);
  and and_28 (and_28_out, and_36_out, j_k_ff_9_q);
  J_K_Flip_Flop j_k_ff_10 (
    .J(and_28_out), .K(and_28_out), .clk(clock_1_out), .Q(j_k_ff_10_q), .Qn(j_k_ff_10_qn), .reset(and_27_out));  // open: preset
  not not_14 (not_14_out, j_k_ff_15_q);
  not not_15 (not_15_out, j_k_ff_16_q);
  not not_16 (not_16_out, j_k_ff_12_q);
  and and_29 (and_29_out, and_28_out, j_k_ff_10_q);
  and and_30 (and_30_out, j_k_ff_11_q, j_k_ff_9_q);
  and and_31 (and_31_out, not_13_out, not_10_out);
  and and_32 (and_32_out, not_16_out, not_13_out);
  and and_33 (and_33_out, not_11_out, not_10_out);
  or or_18 (or_18_out, j_k_ff_12_q, j_k_ff_11_q, not_11_out, j_k_ff_9_q);
  and and_34 (and_34_out, j_k_ff_10_q, not_10_out);
  or or_19 (or_19_out, j_k_ff_11_q, j_k_ff_10_q);
  J_K_Flip_Flop j_k_ff_11 (
    .J(and_29_out), .K(and_29_out), .clk(clock_1_out), .Q(j_k_ff_11_q), .Qn(j_k_ff_11_qn), .reset(and_27_out));  // open: preset
  or P_R (P_R_out, j_k_ff_16_q, j_k_ff_14_q);
  and QS (QS_out, j_k_ff_15_q, j_k_ff_13_q);
  and QaSa (QaSa_out, not_14_out, not_9_out);
  and PaQa (PaQa_out, not_15_out, not_14_out);
  and RaSa (RaSa_out, not_12_out, not_9_out);
  and RS (RS_out, j_k_ff_14_q, j_k_ff_13_q);
  or or_20 (or_20_out, j_k_ff_16_q, j_k_ff_15_q, not_12_out, j_k_ff_13_q);
  and RSa (RSa_out, j_k_ff_14_q, not_9_out);
  and QRa (QRa_out, j_k_ff_15_q, not_12_out);
  and QSa (QSa_out, j_k_ff_15_q, not_9_out);
  or QQ (QQ_out, and_30_out, and_31_out);
  and and_35 (and_35_out, and_29_out, j_k_ff_11_q);
  J_K_Flip_Flop j_k_ff_12 (
    .J(and_35_out), .K(and_35_out), .clk(clock_1_out), .Q(j_k_ff_12_q), .Qn(j_k_ff_12_qn), .reset(and_27_out));  // open: preset
  or or_21 (or_21_out, j_k_ff_10_q, QQ_out);
  or or_22 (or_22_out, and_32_out, and_33_out);
  or or_23 (or_23_out, and_33_out, j_k_ff_11_q);
  or or_24 (or_24_out, and_31_out, and_34_out);
  or or_25 (or_25_out, P_R_out, QS_out, QaSa_out);
  or or_26 (or_26_out, j_k_ff_16_q, PaQa_out, RaSa_out, RS_out);
  or or_27 (or_27_out, QaSa_out, RSa_out);
  or P_RSa (P_RSa_out, j_k_ff_16_q, RSa_out);
  and QRaS (QRaS_out, j_k_ff_13_q, QRa_out);
  and PaQaR (PaQaR_out, PaQa_out, j_k_ff_14_q);
  or or_28 (or_28_out, RaSa_out, j_k_ff_16_q);
  or or_29 (or_29_out, QaSa_out, P_RSa_out, QRaS_out, PaQaR_out);
  or or_30 (or_30_out, P_RSa_out, PaQaR_out, QRa_out);
  or or_31 (or_31_out, or_28_out, QRa_out, QSa_out);
  and and_36 (and_36_out, j_k_ff_16_q, j_k_ff_15_qn, j_k_ff_14_qn, j_k_ff_13_q);
  J_K_Flip_Flop j_k_ff_13 (
    .J(1'b1), .K(1'b1), .clk(clock_1_out), .Q(j_k_ff_13_q), .reset(and_37_out));  // open: Qn, preset
  and and_37 (and_37_out, j_k_ff_14_q, j_k_ff_16_q);
  J_K_Flip_Flop j_k_ff_14 (
    .J(j_k_ff_13_q), .K(j_k_ff_13_q), .clk(clock_1_out), .Q(j_k_ff_14_q), .Qn(j_k_ff_14_qn),
    .reset(and_37_out));  // open: preset
  and and_38 (and_38_out, j_k_ff_13_q, j_k_ff_14_q);
  J_K_Flip_Flop j_k_ff_15 (
    .J(and_38_out), .K(and_38_out), .clk(clock_1_out), .Q(j_k_ff_15_q), .Qn(j_k_ff_15_qn), .reset(and_37_out));  // open: preset
  and and_39 (and_39_out, and_38_out, j_k_ff_15_q);
  J_K_Flip_Flop j_k_ff_16 (
    .J(and_39_out), .K(and_39_out), .clk(clock_1_out), .Q(j_k_ff_16_q), .reset(and_37_out));  // open: Qn, preset

  // Notes on the sheet:
  //   S
  //   R
  //   Q
  //   P
  //   S
  //   Q
  //   R
  //   P
endmodule
