// Logisim project 24h_clock_sm.circ as structural Verilog: 1 circuit, main circuit main
module main (
);

  wire and_1_out, and_2_out, and_3_out, and_4_out, and_5_out, and_6_out, and_7_out, and_8_out, and_9_out,
       and_10_out, and_11_out, and_12_out, and_13_out, and_14_out, and_15_out, and_16_out, and_17_out,
       and_18_out, and_19_out, and_20_out, and_21_out, and_22_out, and_23_out, and_24_out, and_25_out,
       and_26_out, and_27_out, and_28_out, and_29_out, and_30_out, and_31_out, and_32_out, and_33_out,
       and_34_out, and_35_out, and_36_out, and_37_out, and_38_out, and_39_out, and_40_out, and_41_out,
       and_42_out, and_43_out, and_44_out, and_45_out, and_46_out, and_47_out, and_48_out, and_49_out,
       and_50_out, and_51_out, and_52_out, and_53_out, and_54_out, and_55_out, and_56_out, and_57_out,
       and_58_out, and_59_out, clock_1_out, j_k_ff_1_q, j_k_ff_1_qn, j_k_ff_2_q, j_k_ff_2_qn, j_k_ff_3_q,
       j_k_ff_4_q, j_k_ff_4_qn, j_k_ff_5_q, j_k_ff_5_qn, j_k_ff_6_q, j_k_ff_6_qn, j_k_ff_7_q, j_k_ff_7_qn,
       j_k_ff_8_q, j_k_ff_9_q, j_k_ff_10_q, j_k_ff_10_qn, j_k_ff_11_q, j_k_ff_11_qn, j_k_ff_12_q,
       j_k_ff_12_qn, j_k_ff_13_q, j_k_ff_14_q, j_k_ff_15_q, j_k_ff_15_qn, j_k_ff_16_q, j_k_ff_17_q,
       j_k_ff_18_q, j_k_ff_18_qn, j_k_ff_19_q, j_k_ff_19_qn, j_k_ff_20_q, j_k_ff_20_qn, j_k_ff_21_q,
       j_k_ff_21_qn, j_k_ff_22_q, j_k_ff_23_q, j_k_ff_23_qn, not_1_out, not_2_out, not_3_out, not_4_out,
       not_5_out, not_6_out, not_7_out, not_8_out, not_9_out, not_10_out, not_11_out, not_12_out, not_13_out,
       not_14_out, not_15_out, not_16_out, not_17_out, not_18_out, not_19_out, not_20_out, not_21_out,
       not_22_out, not_23_out, or_1_out, or_2_out, or_3_out, or_4_out, or_5_out, or_6_out, or_7_out,
       or_8_out, or_9_out, or_10_out, or_11_out, or_12_out, or_13_out, or_14_out, or_15_out, or_16_out,
       or_17_out, or_18_out, or_19_out, or_20_out, or_21_out, or_22_out, or_23_out, or_24_out, or_25_out,
       or_26_out, or_27_out, or_28_out, or_29_out, or_30_out, or_31_out, or_32_out, or_33_out, or_34_out,
       or_35_out, or_36_out, or_37_out, or_38_out, or_39_out, or_40_out, or_41_out, or_42_out, P_R_out,
       P_RSa_out, PaQa_out, PaQaR_out, QaSa_out, QQ_out, QRa_out, QRaS_out, QS_out, QSa_out, RaSa_out,
       RS_out, RSa_out;

  and and_1 (and_1_out, j_k_ff_7_q, j_k_ff_6_qn, and_22_out, j_k_ff_4_qn, j_k_ff_2_q);
  not not_1 (not_1_out, j_k_ff_2_q);
  or or_1 (or_1_out, and_6_out, and_3_out);
  not not_2 (not_2_out, j_k_ff_4_q);
  not not_3 (not_3_out, j_k_ff_6_q);
  J_K_Flip_Flop j_k_ff_1 (
    .J(and_1_out), .K(and_1_out), .clk(clock_1_out), .Q(j_k_ff_1_q), .Qn(j_k_ff_1_qn), .reset(and_3_out));  // open: preset
  Clock clock_1 (.out(clock_1_out));
  and and_2 (and_2_out, j_k_ff_1_qn, j_k_ff_3_q, j_k_ff_5_qn);
  J_K_Flip_Flop j_k_ff_2 (
    .J(and_22_out), .K(and_22_out), .clk(clock_1_out), .Q(j_k_ff_2_q), .Qn(j_k_ff_2_qn), .reset(or_1_out));  // open: preset
  and and_3 (and_3_out, and_2_out, j_k_ff_7_qn, j_k_ff_6_q, j_k_ff_4_qn, j_k_ff_2_qn);
  _7_Segment_Display #(.decimalPoint("false")) u_7_segment_display_1 (
    .g(j_k_ff_3_q), .f(and_15_out), .a(not_6_out), .b(not_7_out), .e(not_6_out), .d(not_6_out), .c(not_5_out));
  not not_4 (not_4_out, j_k_ff_7_q);
  not not_5 (not_5_out, j_k_ff_3_q);
  not not_6 (not_6_out, j_k_ff_1_q);
  and and_4 (and_4_out, and_1_out, j_k_ff_1_q);
  and and_5 (and_5_out, and_22_out, j_k_ff_2_q);
  and and_6 (and_6_out, j_k_ff_4_q, j_k_ff_7_q);
  _7_Segment_Display u_7_segment_display_2 (
    .g(or_11_out), .f(or_10_out), .a(or_4_out), .b(or_5_out), .e(or_6_out), .d(or_9_out), .c(or_3_out),
    .dp(1'b1));
  or or_2 (or_2_out, j_k_ff_7_q, j_k_ff_4_q);
  and and_7 (and_7_out, j_k_ff_6_q, j_k_ff_2_q);
  and and_8 (and_8_out, not_3_out, not_1_out);
  and and_9 (and_9_out, not_4_out, not_3_out);
  and and_10 (and_10_out, not_2_out, not_1_out);
  and and_11 (and_11_out, j_k_ff_4_q, j_k_ff_2_q);
  or or_3 (or_3_out, j_k_ff_7_q, j_k_ff_6_q, not_2_out, j_k_ff_2_q);
  and and_12 (and_12_out, j_k_ff_4_q, not_1_out);
  and and_13 (and_13_out, j_k_ff_6_q, not_2_out);
  and and_14 (and_14_out, j_k_ff_6_q, not_1_out);
  and and_15 (and_15_out, not_7_out, not_5_out, not_6_out);
  not not_7 (not_7_out, j_k_ff_5_q);
  J_K_Flip_Flop j_k_ff_3 (
    .J(and_4_out), .K(and_4_out), .clk(clock_1_out), .Q(j_k_ff_3_q), .reset(and_3_out));  // open: Qn, preset
  J_K_Flip_Flop j_k_ff_4 (
    .J(and_5_out), .K(and_5_out), .clk(clock_1_out), .Q(j_k_ff_4_q), .Qn(j_k_ff_4_qn), .reset(or_1_out));  // open: preset
  and and_16 (and_16_out, and_4_out, j_k_ff_3_q);
  J_K_Flip_Flop j_k_ff_5 (
    .J(and_16_out), .K(and_16_out), .clk(clock_1_out), .Q(j_k_ff_5_q), .Qn(j_k_ff_5_qn), .reset(and_3_out));  // open: preset
  and and_17 (and_17_out, and_5_out, j_k_ff_4_q);
  J_K_Flip_Flop j_k_ff_6 (
    .J(and_17_out), .K(and_17_out), .clk(clock_1_out), .Q(j_k_ff_6_q), .Qn(j_k_ff_6_qn), .reset(or_1_out));  // open: preset
  or or_4 (or_4_out, or_2_out, and_7_out, and_8_out);
  or or_5 (or_5_out, j_k_ff_7_q, and_9_out, and_10_out, and_11_out);
  or or_6 (or_6_out, and_8_out, and_12_out);
  or or_7 (or_7_out, j_k_ff_7_q, and_12_out);
  and and_18 (and_18_out, j_k_ff_2_q, and_13_out);
  and and_19 (and_19_out, and_9_out, j_k_ff_4_q);
  or or_8 (or_8_out, and_10_out, j_k_ff_7_q);
  and and_20 (and_20_out, and_17_out, j_k_ff_6_q);
  or or_9 (or_9_out, and_8_out, or_7_out, and_19_out, and_18_out);
  or or_10 (or_10_out, or_8_out, and_13_out, and_14_out);
  J_K_Flip_Flop j_k_ff_7 (
    .J(and_20_out), .K(and_20_out), .clk(clock_1_out), .Q(j_k_ff_7_q), .Qn(j_k_ff_7_qn), .reset(or_1_out));  // open: preset
  or or_11 (or_11_out, or_7_out, and_19_out, and_13_out);
  not not_8 (not_8_out, j_k_ff_8_q);
  _7_Segment_Display #(.decimalPoint("false")) u_7_segment_display_3 (
    .g(or_13_out), .f(or_16_out), .a(or_20_out), .b(or_15_out), .e(or_17_out), .d(or_20_out), .c(or_12_out));
  not not_9 (not_9_out, j_k_ff_13_q);
  not not_10 (not_10_out, j_k_ff_11_q);
  not not_11 (not_11_out, j_k_ff_9_q);
  and and_21 (and_21_out, j_k_ff_14_q, j_k_ff_12_qn, and_46_out, j_k_ff_10_qn, j_k_ff_9_q);
  and and_22 (and_22_out, and_21_out, j_k_ff_15_qn, j_k_ff_11_qn, j_k_ff_13_q, j_k_ff_8_q);
  _7_Segment_Display u_7_segment_display_4 (
    .g(or_27_out), .f(or_28_out), .a(or_21_out), .b(or_22_out), .e(or_23_out), .d(or_26_out), .c(or_19_out),
    .dp(1'b1));
  not not_12 (not_12_out, j_k_ff_15_q);
  not not_13 (not_13_out, j_k_ff_10_q);
  J_K_Flip_Flop j_k_ff_8 (
    .J(and_21_out), .K(and_21_out), .clk(clock_1_out), .Q(j_k_ff_8_q), .reset(and_39_out));  // open: Qn, preset
  and and_23 (and_23_out, j_k_ff_13_q, j_k_ff_8_q);
  and and_24 (and_24_out, not_9_out, not_8_out);
  and and_25 (and_25_out, not_12_out, not_9_out);
  and and_26 (and_26_out, not_10_out, not_8_out);
  or or_12 (or_12_out, j_k_ff_15_q, j_k_ff_13_q, not_10_out, j_k_ff_8_q);
  and and_27 (and_27_out, j_k_ff_11_q, not_8_out);
  or or_13 (or_13_out, j_k_ff_13_q, j_k_ff_11_q);
  not not_14 (not_14_out, j_k_ff_12_q);
  not not_15 (not_15_out, j_k_ff_14_q);
  J_K_Flip_Flop j_k_ff_9 (
    .J(and_46_out), .K(and_46_out), .clk(clock_1_out), .Q(j_k_ff_9_q), .reset(and_28_out));  // open: Qn, preset
  and and_28 (and_28_out, j_k_ff_10_q, j_k_ff_14_q);
  or or_14 (or_14_out, and_23_out, and_24_out);
  or or_15 (or_15_out, and_25_out, and_26_out);
  or or_16 (or_16_out, and_26_out, j_k_ff_13_q);
  or or_17 (or_17_out, and_24_out, and_27_out);
  or or_18 (or_18_out, j_k_ff_14_q, j_k_ff_10_q);
  and and_29 (and_29_out, j_k_ff_12_q, j_k_ff_9_q);
  and and_30 (and_30_out, not_14_out, not_11_out);
  and and_31 (and_31_out, not_15_out, not_14_out);
  and and_32 (and_32_out, not_13_out, not_11_out);
  and and_33 (and_33_out, j_k_ff_10_q, j_k_ff_9_q);
  or or_19 (or_19_out, j_k_ff_14_q, j_k_ff_12_q, not_13_out, j_k_ff_9_q);
  and and_34 (and_34_out, j_k_ff_10_q, not_11_out);
  and and_35 (and_35_out, j_k_ff_12_q, not_13_out);
  and and_36 (and_36_out, j_k_ff_12_q, not_11_out);
  and and_37 (and_37_out, and_46_out, j_k_ff_9_q);
  J_K_Flip_Flop j_k_ff_10 (
    .J(and_37_out), .K(and_37_out), .clk(clock_1_out), .Q(j_k_ff_10_q), .Qn(j_k_ff_10_qn), .reset(and_28_out));  // open: preset
  and and_38 (and_38_out, and_21_out, j_k_ff_8_q);
  and and_39 (and_39_out, j_k_ff_11_q, j_k_ff_13_q);
  or or_20 (or_20_out, j_k_ff_11_q, or_14_out);
  J_K_Flip_Flop j_k_ff_11 (
    .J(and_38_out), .K(and_38_out), .clk(clock_1_out), .Q(j_k_ff_11_q), .Qn(j_k_ff_11_qn), .reset(and_39_out));  // open: preset
  or or_21 (or_21_out, or_18_out, and_29_out, and_30_out);
  or or_22 (or_22_out, j_k_ff_14_q, and_31_out, and_32_out, and_33_out);
  or or_23 (or_23_out, and_30_out, and_34_out);
  or or_24 (or_24_out, j_k_ff_14_q, and_34_out);
  and and_40 (and_40_out, j_k_ff_9_q, and_35_out);
  and and_41 (and_41_out, and_31_out, j_k_ff_10_q);
  or or_25 (or_25_out, and_32_out, j_k_ff_14_q);
  and and_42 (and_42_out, and_37_out, j_k_ff_10_q);
  J_K_Flip_Flop j_k_ff_12 (
    .J(and_42_out), .K(and_42_out), .clk(clock_1_out), .Q(j_k_ff_12_q), .Qn(j_k_ff_12_qn), .reset(and_28_out));  // open: preset
  and and_43 (and_43_out, and_38_out, j_k_ff_11_q);
  J_K_Flip_Flop j_k_ff_13 (
    .J(and_43_out), .K(and_43_out), .clk(clock_1_out), .Q(j_k_ff_13_q), .reset(and_39_out));  // open: Qn, preset
  or or_26 (or_26_out, and_30_out, or_24_out, and_41_out, and_40_out);
  or or_27 (or_27_out, or_24_out, and_41_out, and_35_out);
  or or_28 (or_28_out, or_25_out, and_35_out, and_36_out);
  and and_44 (and_44_out, and_42_out, j_k_ff_12_q);
  and and_45 (and_45_out, and_43_out, j_k_ff_13_q);
  J_K_Flip_Flop j_k_ff_14 (
    .J(and_44_out), .K(and_44_out), .clk(clock_1_out), .Q(j_k_ff_14_q), .reset(and_28_out));  // open: Qn, preset
  J_K_Flip_Flop j_k_ff_15 (
    .J(and_45_out), .K(and_45_out), .clk(clock_1_out), .Q(j_k_ff_15_q), .Qn(j_k_ff_15_qn), .reset(and_39_out));  // open: preset
  _7_Segment_Display #(.decimalPoint("false")) u_7_segment_display_5 (
    .g(or_31_out), .f(or_33_out), .a(or_39_out), .b(or_32_out), .e(or_34_out), .d(or_39_out), .c(or_30_out));
  _7_Segment_Display #(.decimalPoint("false")) u_7_segment_display_6 (
    .g(or_41_out), .f(or_42_out), .a(or_35_out), .b(or_36_out), .e(or_37_out), .d(or_40_out), .c(or_29_out));
  and and_46 (and_46_out, j_k_ff_23_qn, j_k_ff_21_q, and_47_out, j_k_ff_19_qn, j_k_ff_17_q);
  and and_47 (and_47_out, j_k_ff_22_q, j_k_ff_20_qn, j_k_ff_18_qn, j_k_ff_16_q);
  J_K_Flip_Flop j_k_ff_16 (
    .J(1'b1), .K(1'b1), .clk(clock_1_out), .Q(j_k_ff_16_q), .reset(and_48_out));  // open: Qn, preset
  J_K_Flip_Flop j_k_ff_17 (
    .J(and_47_out), .K(and_47_out), .clk(clock_1_out), .Q(j_k_ff_17_q), .reset(and_50_out));  // open: Qn, preset
  and and_48 (and_48_out, j_k_ff_18_q, j_k_ff_22_q);
  not not_16 (not_16_out, j_k_ff_16_q);
  not not_17 (not_17_out, j_k_ff_17_q);
  and and_49 (and_49_out, and_47_out, j_k_ff_17_q);
  and and_50 (and_50_out, j_k_ff_19_q, j_k_ff_21_q);
  J_K_Flip_Flop j_k_ff_18 (
    .J(j_k_ff_16_q), .K(j_k_ff_16_q), .clk(clock_1_out), .Q(j_k_ff_18_q), .Qn(j_k_ff_18_qn),
    .reset(and_48_out));  // open: preset
  not not_18 (not_18_out, j_k_ff_18_q);
  not not_19 (not_19_out, j_k_ff_20_q);
  not not_20 (not_20_out, j_k_ff_19_q);
  not not_21 (not_21_out, j_k_ff_21_q);
  J_K_Flip_Flop j_k_ff_19 (
    .J(and_49_out), .K(and_49_out), .clk(clock_1_out), .Q(j_k_ff_19_q), .Qn(j_k_ff_19_qn), .reset(and_50_out));  // open: preset
  and and_51 (and_51_out, j_k_ff_16_q, j_k_ff_18_q);
  J_K_Flip_Flop j_k_ff_20 (
    .J(and_51_out), .K(and_51_out), .clk(clock_1_out), .Q(j_k_ff_20_q), .Qn(j_k_ff_20_qn), .reset(and_48_out));  // open: preset
  not not_22 (not_22_out, j_k_ff_22_q);
  not not_23 (not_23_out, j_k_ff_23_q);
  and and_52 (and_52_out, and_49_out, j_k_ff_19_q);
  J_K_Flip_Flop j_k_ff_21 (
    .J(and_52_out), .K(and_52_out), .clk(clock_1_out), .Q(j_k_ff_21_q), .Qn(j_k_ff_21_qn), .reset(and_50_out));  // open: preset
  or P_R (P_R_out, j_k_ff_22_q, j_k_ff_18_q);
  and QS (QS_out, j_k_ff_20_q, j_k_ff_16_q);
  and QaSa (QaSa_out, not_19_out, not_16_out);
  and PaQa (PaQa_out, not_22_out, not_19_out);
  and RaSa (RaSa_out, not_18_out, not_16_out);
  and RS (RS_out, j_k_ff_18_q, j_k_ff_16_q);
  or or_29 (or_29_out, j_k_ff_22_q, j_k_ff_20_q, not_18_out, j_k_ff_16_q);
  and RSa (RSa_out, j_k_ff_18_q, not_16_out);
  and QRa (QRa_out, j_k_ff_20_q, not_18_out);
  and QSa (QSa_out, j_k_ff_20_q, not_16_out);
  and and_53 (and_53_out, j_k_ff_21_q, j_k_ff_17_q);
  and and_54 (and_54_out, not_21_out, not_17_out);
  and and_55 (and_55_out, not_23_out, not_21_out);
  and and_56 (and_56_out, not_20_out, not_17_out);
  or or_30 (or_30_out, j_k_ff_23_q, j_k_ff_21_q, not_20_out, j_k_ff_17_q);
  and and_57 (and_57_out, j_k_ff_19_q, not_17_out);
  or or_31 (or_31_out, j_k_ff_21_q, j_k_ff_19_q);
  and and_58 (and_58_out, and_52_out, j_k_ff_21_q);
  and and_59 (and_59_out, and_51_out, j_k_ff_20_q);
  J_K_Flip_Flop j_k_ff_22 (
    .J(and_59_out), .K(and_59_out), .clk(clock_1_out), .Q(j_k_ff_22_q), .reset(and_48_out));  // open: Qn, preset
  or QQ (QQ_out, and_53_out, and_54_out);
  or or_32 (or_32_out, and_55_out, and_56_out);
  or or_33 (or_33_out, and_56_out, j_k_ff_21_q);
  or or_34 (or_34_out, and_54_out, and_57_out);
  J_K_Flip_Flop j_k_ff_23 (
    .K(and_58_out), .clk(clock_1_out), .Q(j_k_ff_23_q), .Qn(j_k_ff_23_qn), .reset(and_50_out));  // open: J, preset
  or or_35 (or_35_out, P_R_out, QS_out, QaSa_out);
  or or_36 (or_36_out, j_k_ff_22_q, PaQa_out, RaSa_out, RS_out);
  or or_37 (or_37_out, QaSa_out, RSa_out);
  or P_RSa (P_RSa_out, j_k_ff_22_q, RSa_out);
  and QRaS (QRaS_out, j_k_ff_16_q, QRa_out);
  and PaQaR (PaQaR_out, PaQa_out, j_k_ff_18_q);
  or or_38 (or_38_out, RaSa_out, j_k_ff_22_q);
  or or_39 (or_39_out, j_k_ff_19_q, QQ_out);
  or or_40 (or_40_out, QaSa_out, P_RSa_out, PaQaR_out, QRaS_out);
  or or_41 (or_41_out, P_RSa_out, PaQaR_out, QRa_out);
  or or_42 (or_42_out, or_38_out, QRa_out, QSa_out);

  // Notes on the sheet:
  //   S
  //   R
  //   Q
  //   P
  //   S
  //   Q
  //   R
  //   P
  //   S
  //   R
  //   Q
  //   P
endmodule
