// Logisim project counters_x.circ as structural Verilog: 1 circuit, main circuit main
module main (
);

  wire and_1_out, and_2_out, and_3_out, and_4_out, and_5_out, and_6_out, and_7_out, and_8_out, and_9_out,
       and_10_out, and_11_out, and_12_out, and_13_out, clock_1_out, clock_2_out, clock_3_out, clock_4_out,
       j_k_ff_1_q, j_k_ff_2_q, j_k_ff_3_q, j_k_ff_4_q, j_k_ff_5_q, j_k_ff_6_q, j_k_ff_7_q, j_k_ff_8_q,
       j_k_ff_9_q, j_k_ff_12_q, j_k_ff_13_q, j_k_ff_14_q, j_k_ff_14_qn, j_k_ff_15_q, j_k_ff_16_q,
       j_k_ff_17_q, j_k_ff_18_q, j_k_ff_18_qn, j_k_ff_19_q, j_k_ff_19_qn, j_k_ff_20_q;

  J_K_Flip_Flop j_k_ff_1 (.J(1'b1), .K(1'b1), .clk(clock_1_out), .Q(j_k_ff_1_q));  // open: Qn, preset, reset
  Clock clock_1 (.out(clock_1_out));
  J_K_Flip_Flop j_k_ff_2 (.J(1'b1), .K(1'b1), .clk(clock_2_out), .Q(j_k_ff_2_q));  // open: Qn, preset, reset
  Clock clock_2 (.out(clock_2_out));
  J_K_Flip_Flop j_k_ff_3 (
    .J(1'b1), .K(1'b1), .clk(clock_3_out), .Q(j_k_ff_3_q), .reset(and_1_out));  // open: Qn, preset
  Clock clock_3 (.out(clock_3_out));
  and and_1 (and_1_out, j_k_ff_6_q, j_k_ff_12_q);
  J_K_Flip_Flop j_k_ff_4 (.J(1'b1), .K(1'b1), .clk(j_k_ff_1_q), .Q(j_k_ff_4_q));  // open: Qn, preset, reset
  J_K_Flip_Flop j_k_ff_5 (
    .J(j_k_ff_2_q), .K(j_k_ff_2_q), .clk(clock_2_out), .Q(j_k_ff_5_q));  // open: Qn, preset, reset
  J_K_Flip_Flop j_k_ff_6 (
    .J(j_k_ff_3_q), .K(j_k_ff_3_q), .clk(clock_3_out), .Q(j_k_ff_6_q), .reset(and_1_out));  // open: Qn, preset
  J_K_Flip_Flop j_k_ff_7 (.J(1'b1), .K(1'b1), .clk(j_k_ff_4_q), .Q(j_k_ff_7_q));  // open: Qn, preset, reset
  and and_2 (and_2_out, j_k_ff_2_q, j_k_ff_5_q);
  and and_3 (and_3_out, j_k_ff_3_q, j_k_ff_6_q);
  J_K_Flip_Flop j_k_ff_8 (.J(and_2_out), .K(and_2_out), .clk(clock_2_out), .Q(j_k_ff_8_q));  // open: Qn, preset, reset
  J_K_Flip_Flop j_k_ff_9 (
    .J(and_3_out), .K(and_3_out), .clk(clock_3_out), .Q(j_k_ff_9_q), .reset(and_1_out));  // open: Qn, preset
  J_K_Flip_Flop j_k_ff_10 (.J(1'b1), .K(1'b1), .clk(j_k_ff_7_q));  // open: Q, Qn, preset, reset
  and and_4 (and_4_out, and_2_out, j_k_ff_8_q);
  J_K_Flip_Flop j_k_ff_11 (.J(and_4_out), .K(and_4_out), .clk(clock_2_out));  // open: Q, Qn, preset, reset
  and and_5 (and_5_out, and_3_out, j_k_ff_9_q);
  J_K_Flip_Flop j_k_ff_12 (
    .J(and_5_out), .K(and_5_out), .clk(clock_3_out), .Q(j_k_ff_12_q), .reset(and_1_out));  // open: Qn, preset
  J_K_Flip_Flop j_k_ff_13 (
    .J(and_10_out), .K(and_10_out), .clk(clock_4_out), .Q(j_k_ff_13_q), .reset(and_6_out));  // open: Qn, preset
  Clock clock_4 (.out(clock_4_out));
  and and_6 (and_6_out, j_k_ff_14_q, j_k_ff_16_q);
  and and_7 (and_7_out, and_10_out, j_k_ff_13_q);
  J_K_Flip_Flop j_k_ff_14 (
    .J(and_7_out), .K(and_7_out), .clk(clock_4_out), .Q(j_k_ff_14_q), .Qn(j_k_ff_14_qn), .reset(and_6_out));  // open: preset
  and and_8 (and_8_out, and_7_out, j_k_ff_14_q);
  J_K_Flip_Flop j_k_ff_15 (
    .J(and_8_out), .K(and_8_out), .clk(clock_4_out), .Q(j_k_ff_15_q), .reset(and_6_out));  // open: Qn, preset
  and and_9 (and_9_out, and_8_out, j_k_ff_15_q);
  J_K_Flip_Flop j_k_ff_16 (
    .J(and_9_out), .K(and_9_out), .clk(clock_4_out), .Q(j_k_ff_16_q), .reset(and_6_out));  // open: Qn, preset
  and and_10 (and_10_out, j_k_ff_20_q, j_k_ff_19_qn, j_k_ff_18_qn, j_k_ff_17_q);
  J_K_Flip_Flop j_k_ff_17 (
    .J(1'b1), .K(1'b1), .clk(clock_4_out), .Q(j_k_ff_17_q), .reset(and_11_out));  // open: Qn, preset
  and and_11 (and_11_out, j_k_ff_18_q, j_k_ff_20_q);
  J_K_Flip_Flop j_k_ff_18 (
    .J(j_k_ff_17_q), .K(j_k_ff_17_q), .clk(clock_4_out), .Q(j_k_ff_18_q), .Qn(j_k_ff_18_qn),
    .reset(and_11_out));  // open: preset
  and and_12 (and_12_out, j_k_ff_17_q, j_k_ff_18_q);
  J_K_Flip_Flop j_k_ff_19 (
    .J(and_12_out), .K(and_12_out), .clk(clock_4_out), .Q(j_k_ff_19_q), .Qn(j_k_ff_19_qn), .reset(and_11_out));  // open: preset
  and and_13 (and_13_out, and_12_out, j_k_ff_19_q);
  J_K_Flip_Flop j_k_ff_20 (
    .J(and_13_out), .K(and_13_out), .clk(clock_4_out), .Q(j_k_ff_20_q), .reset(and_11_out));  // open: Qn, preset

  // Notes on the sheet:
  //   JK Ripple Down Counter
  //   JK Sync Up Counter
  //   JK Sync BCD Up Counter
  //   2 JK Sync BCD Up Counter
endmodule
