// Logisim project 2_decoder_sm.circ as structural Verilog: 1 circuit, main circuit main
module main (
  input  S,
  input  R,
  input  Q,
  input  P,
  output A,
  output B,
  output C,
  output D,
  output E,
  output F,
  output G
);

  wire not_3_out;

  not not_1 (A, S);
  not not_2 (C, P);
  not not_3 (not_3_out, P);
  and and_1 (B, not_3_out, Q);
  and and_2 (F, C, A);

  assign D = A;
  assign E = A;
  assign G = P;
  assign R = P;
endmodule
