// Logisim project 6_decoder.circ as structural Verilog: 1 circuit, main circuit main
module main (
  input  S,
  input  R,
  input  Q,
  input  P,
  output A,
  output B,
  output C,
  output D,
  output E,
  output F,
  output G
);

  wire and_1_out, and_2_out, not_1_out, not_2_out, not_3_out, not_4_out, PaQ_out, QaSa_out, QS_out;

  not not_1 (not_1_out, S);
  not not_2 (not_2_out, R);
  not not_3 (not_3_out, Q);
  not not_4 (not_4_out, P);
  and QaSa (QaSa_out, not_3_out, not_1_out);
  and QS (QS_out, not_3_out, S);
  or or_1 (C, P, Q, not_2_out, S);
  and and_1 (and_1_out, R, not_1_out);
  and and_2 (and_2_out, not_2_out, not_1_out);
  and PaQ (PaQ_out, not_4_out, Q);
  or or_2 (A, P, R, QaSa_out, QS_out);
  or or_3 (B, P, not_3_out, R, S);
  or or_4 (D, QaSa_out, QS_out, R);
  or or_5 (E, QaSa_out, QS_out, and_1_out);
  or or_6 (F, and_2_out, PaQ_out);
  or or_7 (G, PaQ_out, R);
endmodule
