// Logisim project 6_decoder_sm.circ as structural Verilog: 1 circuit, main circuit main
module main (
  input  S,
  input  R,
  input  Q,
  input  P,
  output A,
  output B,
  output C,
  output D,
  output E,
  output F,
  output G
);

  wire not_1_out, not_2_out, not_3_out, not_4_out, PaQa_out, QaSa_out, QQ_out, QS_out, RaSa_out, RSa_out;

  not not_1 (not_1_out, S);
  not not_2 (not_2_out, R);
  not not_3 (not_3_out, Q);
  not not_4 (not_4_out, P);
  and QS (QS_out, Q, S);
  and QaSa (QaSa_out, not_3_out, not_1_out);
  and PaQa (PaQa_out, not_4_out, not_3_out);
  and RaSa (RaSa_out, not_2_out, not_1_out);
  or or_1 (C, P, Q, not_2_out, S);
  and RSa (RSa_out, R, not_1_out);
  or or_2 (G, Q, R);
  or QQ (QQ_out, QS_out, QaSa_out);
  or or_3 (B, PaQa_out, RaSa_out);
  or or_4 (F, RaSa_out, Q);
  or or_5 (E, QaSa_out, RSa_out);
  or or_6 (A, R, QQ_out);

  assign D = A;
endmodule
