// Logisim project bcd_decoder_sm.circ as structural Verilog: 1 circuit, main circuit main
module main (
  input  S,
  input  R,
  input  Q,
  input  P,
  output A,
  output B,
  output C,
  output D,
  output E,
  output F,
  output G
);

  wire not_1_out, not_2_out, not_3_out, not_4_out, or_5_out, P_R_out, P_RSa_out, PaQa_out, PaQaR_out,
       QaSa_out, QRa_out, QRaS_out, QS_out, QSa_out, RaSa_out, RS_out, RSa_out;

  not not_1 (not_1_out, S);
  not not_2 (not_2_out, R);
  not not_3 (not_3_out, Q);
  not not_4 (not_4_out, P);
  or P_R (P_R_out, P, R);
  and QS (QS_out, Q, S);
  and QaSa (QaSa_out, not_3_out, not_1_out);
  and PaQa (PaQa_out, not_4_out, not_3_out);
  and RaSa (RaSa_out, not_2_out, not_1_out);
  and RS (RS_out, R, S);
  or or_1 (C, P, Q, not_2_out, S);
  and RSa (RSa_out, R, not_1_out);
  and QRa (QRa_out, Q, not_2_out);
  and QSa (QSa_out, Q, not_1_out);
  or or_2 (A, P_R_out, QS_out, QaSa_out);
  or or_3 (B, P, PaQa_out, RaSa_out, RS_out);
  or or_4 (E, QaSa_out, RSa_out);
  or P_RSa (P_RSa_out, P, RSa_out);
  and QRaS (QRaS_out, S, QRa_out);
  and PaQaR (PaQaR_out, PaQa_out, R);
  or or_5 (or_5_out, RaSa_out, P);
  or or_6 (D, QaSa_out, P_RSa_out, PaQaR_out, QRaS_out);
  or or_7 (G, P_RSa_out, PaQaR_out, QRa_out);
  or or_8 (F, or_5_out, QRa_out, QSa_out);

  // Notes on the sheet:
  //   S
  //   R
  //   Q
  //   P
endmodule
