// Logisim project size_comparison.circ as structural Verilog: 1 circuit, main circuit main
module main (
  input  in_1,
  input  in_2,
  input  in_3,
  input  in_4,
  input  S,
  input  R,
  input  Q,
  input  P,
  input  in_9,
  input  in_10,
  input  in_11,
  input  in_12,
  output out_13,
  output out_14,
  output out_15,
  output out_16,
  output out_17,
  output out_18,
  output out_19,
  output A,
  output B,
  output C,
  output D,
  output E,
  output F,
  output G,
  output out_27,
  output out_28,
  output out_29,
  output out_30,
  output out_31,
  output out_32,
  output out_33
);

  wire and_3_out, and_4_out, and_5_out, and_6_out, and_7_out, and_8_out, and_9_out, clock_1_out, j_k_ff_1_q,
       j_k_ff_2_q, j_k_ff_3_q, j_k_ff_4_q, not_3_out, not_4_out, not_5_out, not_6_out, not_7_out, not_8_out,
       not_9_out, not_10_out, not_11_out, or_12_out, P_R_out, P_RSa_out, PaQ_out, PaQa_out, PaQaR_out,
       QaSa_out, QRa_out, QRaS_out, QS_out, QSa_out, RaSa_out, RS_out, RSa_out;

  not not_1 (out_27, in_9);
  not not_2 (out_29, in_10);
  not not_3 (not_3_out, in_10);
  and and_1 (out_28, not_3_out, in_11);
  and and_2 (out_32, out_29, out_27);
  _7_Segment_Display u_7_segment_display_1 ();  // open: g, f, a, b, e, d, c, dp
  not not_4 (not_4_out, in_1);
  not not_5 (not_5_out, in_2);
  not not_6 (not_6_out, in_3);
  J_K_Flip_Flop j_k_ff_1 (
    .J(1'b1), .K(1'b1), .clk(clock_1_out), .Q(j_k_ff_1_q), .reset(and_3_out));  // open: Qn, preset
  Clock clock_1 (.out(clock_1_out));
  not not_7 (not_7_out, in_4);
  and and_3 (and_3_out, j_k_ff_2_q, j_k_ff_4_q);
  and and_4 (and_4_out, not_6_out, not_4_out);
  and and_5 (and_5_out, not_7_out, not_6_out);
  or or_1 (out_15, in_4, in_3, not_5_out, in_1);
  and and_6 (and_6_out, in_2, not_4_out);
  and and_7 (and_7_out, not_5_out, not_4_out);
  and PaQ (PaQ_out, not_7_out, in_3);
  J_K_Flip_Flop j_k_ff_2 (
    .J(j_k_ff_1_q), .K(j_k_ff_1_q), .clk(clock_1_out), .Q(j_k_ff_2_q), .reset(and_3_out));  // open: Qn, preset
  and and_8 (and_8_out, j_k_ff_1_q, j_k_ff_2_q);
  J_K_Flip_Flop j_k_ff_3 (
    .J(and_8_out), .K(and_8_out), .clk(clock_1_out), .Q(j_k_ff_3_q), .reset(and_3_out));  // open: Qn, preset
  or or_2 (out_13, in_4, in_2, and_4_out);
  or or_3 (out_14, not_5_out, and_5_out);
  or or_4 (out_16, and_4_out, in_2);
  or or_5 (out_17, and_4_out, and_6_out);
  or or_6 (out_18, and_7_out, PaQ_out);
  or or_7 (out_19, PaQ_out, in_2);
  and and_9 (and_9_out, and_8_out, j_k_ff_3_q);
  J_K_Flip_Flop j_k_ff_4 (
    .J(and_9_out), .K(and_9_out), .clk(clock_1_out), .Q(j_k_ff_4_q), .reset(and_3_out));  // open: Qn, preset
  not not_8 (not_8_out, S);
  not not_9 (not_9_out, R);
  not not_10 (not_10_out, Q);
  not not_11 (not_11_out, P);
  or P_R (P_R_out, P, R);
  and QS (QS_out, Q, S);
  and QaSa (QaSa_out, not_10_out, not_8_out);
  and PaQa (PaQa_out, not_11_out, not_10_out);
  and RaSa (RaSa_out, not_9_out, not_8_out);
  and RS (RS_out, R, S);
  or or_8 (C, P, Q, not_9_out, S);
  and RSa (RSa_out, R, not_8_out);
  and QRa (QRa_out, Q, not_9_out);
  and QSa (QSa_out, Q, not_8_out);
  or or_9 (A, P_R_out, QS_out, QaSa_out);
  or or_10 (B, P, PaQa_out, RaSa_out, RS_out);
  or or_11 (E, QaSa_out, RSa_out);
  or P_RSa (P_RSa_out, P, RSa_out);
  and QRaS (QRaS_out, S, QRa_out);
  and PaQaR (PaQaR_out, PaQa_out, R);
  or or_12 (or_12_out, RaSa_out, P);
  or or_13 (D, QaSa_out, P_RSa_out, QRaS_out, PaQaR_out);
  or or_14 (F, or_12_out, QRa_out, QSa_out);
  or or_15 (G, P_RSa_out, PaQaR_out, QRa_out);

  assign in_12 = in_10;
  assign out_30 = out_27;
  assign out_31 = out_27;
  assign out_33 = in_10;

  // Notes on the sheet:
  //   S
  //   R
  //   Q
  //   P
endmodule
